# Fritzing sketch layout (saved by Fritzing 0.9.3b)
breadboards: 1

parts:
  Part1 = Arduino Uno (Rev3)
  Part2 = Logic Level Converter
  Part3 = VEML6070 [part_number=VEML6070]
  Part5 = Digital Temperature Sensor Breakout - TMP102
  Part6 = Adafruit TSL2561 [part_number="Adafruit #439"]

nets:
  N1: Part1.A4/SDA, Part2.RX2_HV
  N2: Part1.A5/SCL, Part2.TX2_HV
  GND: Part1.GND, Part2.GND, Part3.GND, Part5.GND, Part5.ADD0, Part6.GND, Part6.ADDR
  N3: Part1.5V, Part2.HV
  N4: Part2.TX2_LV, Part3.SCL, Part5.SCL, Part6.SCL
  N5: Part2.RX2_LV, Part3.SDA, Part5.SDA, Part6.SDA
  VDD: Part2.LV, Part3.VDD, Part5.V+, Part6.VIN

custom parts:
  VEML6070: This little sensor is a great way to add UV light sensing to any microcontroller project. The VEML6070 from Vishay has a true UV A light sensor and an I2C-controlled ADC that will take readings and integrate them for you over ~60ms to 500ms.
  Adafruit TSL2561: The TSL2561 luminosity sensor is an advanced digital light sensor, ideal for use in a wide range of light situations. Compared to low cost CdS cells, this sensor is more precise, allowing for exact lux calculations and can be configured for different gain/timing ranges to detect light ranges from up to 0.1 - 40,000+ Lux on the fly. The best part of this sensor is that it contains both infrared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
